// Logisim project FPGA.circ as structural Verilog: 2 circuits, main circuit FPGA_G3-G4
module FPGA_G3_G4 (
  input  E0,
  input  E1
);

  wire not_1_out, undriven;

  nor nor_1 (E0, not_1_out, undriven);
  and and_1 (E1, not_1_out, undriven);
  not not_1 (not_1_out, undriven);
  Clock CLK ();  // open: out
endmodule

module FPGA_G1_G2 (
  input  BTN2_2NEG,
  input  BTN2_NEG,
  output E2,
  output E3
);

  wire not_1_out;

  nor nor_1 (E2, BTN2_2NEG, BTN2_NEG);
  and and_1 (E3, not_1_out, BTN2_NEG);
  not not_1 (not_1_out, BTN2_NEG);
  not not_2 (BTN2_2NEG, not_1_out);
  Button BTN2 ();  // open: out
endmodule
